// Logisim project Game.circ as structural Verilog: 1 circuit, main circuit main
module main (
  input  [1:0] in_1,
  input  in_2,
  input  [1:0] in_3,
  output [3:0] out_4
);

  wire and_2_out, button_1_out, clk, clock_1_out, comparator_1_eq, comparator_3_eq, comparator_3_lt, crash,
       isless, not_1_out, not_2_out, or_1_out;
  wire [1:0] A, adder_1_out, B, C, counter_1_q, D, E, F, G, H, I, J, K, L, M, multiplexer_1_out,
       multiplexer_2_out, N, O, P, random_1_out, random_2_out, shift_register_2_q1;
  wire [3:0] bit_extender_15_out;
  wire [7:0] bit_extender_1_out, bit_extender_2_out, bit_extender_3_out, bit_extender_4_out,
       bit_extender_5_out, bit_extender_6_out, bit_extender_7_out, bit_extender_8_out, bit_extender_9_out,
       bit_extender_10_out, bit_extender_11_out, bit_extender_12_out, bit_extender_13_out,
       bit_extender_14_out, Memo;
  wire [7:4] counter_2_q;

  Clock clock_1 (.out(clock_1_out));
  Counter #(.width(2), .max('h1)) counter_1 (.Q(counter_1_q), .clk(clk));  // open: load, D, count, carry, clr
  not not_1 (not_1_out, isless);
  and and_1 (clk, not_1_out, clock_1_out);
  or or_1 (or_1_out, isless, crash);
  Multiplexer #(.width(2)) multiplexer_1 (
    .in0(in_1), .in1(2'b10), .out(multiplexer_1_out), .sel(button_1_out));  // open: en
  Random #(.width(2)) random_1 (.clk(clk), .out(random_1_out));  // open: next, clr
  Random #(.width(2), .trigger("falling")) random_2 (.clk(clk), .out(random_2_out));  // open: next, clr
  Shift_Register #(.width(2), .length(15), .trigger("falling")) shift_register_1 (
    .in(multiplexer_2_out), .clk(clk), .out(A), .clr(or_1_out), .q0(P), .q1(O), .q2(N), .q3(M), .q4(L),
    .q5(K), .q6(J), .q7(I), .q8(H), .q9(G), .q10(F), .q11(E), .q12(D), .q13(C), .q14(B));  // open: shift, load, d0, d1, d2, d3, d4, d5, d6, d7, d8, d9, d10, d11, d12, d13, d14
  and and_2 (and_2_out, in_2, not_1_out);
  Comparator #(.width(2)) comparator_1 (.a(random_1_out), .b(random_2_out), .eq(comparator_1_eq));  // open: gt, lt
  Adder #(.width(2)) adder_1 (.a(multiplexer_1_out), .b(counter_1_q), .out(adder_1_out));  // open: cin, cout
  ROM #(.addrWidth(2)) rom_1 (.addr(adder_1_out), .data(Memo), .sel(and_2_out));
  Multiplexer #(.width(2)) multiplexer_2 (
    .in0(random_2_out), .in1(in_3), .out(multiplexer_2_out), .sel(comparator_1_eq));  // open: en
  assign bit_extender_1_out = {{6{1'b0}}, B};  // Bit_Extender bit_extender_1
  assign bit_extender_2_out = {{6{1'b0}}, C};  // Bit_Extender bit_extender_2
  assign bit_extender_3_out = {{6{1'b0}}, D};  // Bit_Extender bit_extender_3
  assign bit_extender_4_out = {{6{1'b0}}, E};  // Bit_Extender bit_extender_4
  assign bit_extender_5_out = {{6{1'b0}}, H};  // Bit_Extender bit_extender_5
  assign bit_extender_6_out = {{6{1'b0}}, M};  // Bit_Extender bit_extender_6
  Counter counter_2 (
    .count(button_1_out), .Q({counter_2_q, out_4}), .clk(clk), .clr(not_2_out));  // open: load, D, carry
  not not_2 (not_2_out, button_1_out);
  Button button_1 (.out(button_1_out));
  assign bit_extender_7_out = {{6{1'b0}}, F};  // Bit_Extender bit_extender_7
  assign bit_extender_8_out = {{6{1'b0}}, G};  // Bit_Extender bit_extender_8
  assign bit_extender_9_out = {{6{1'b0}}, I};  // Bit_Extender bit_extender_9
  assign bit_extender_10_out = {{6{1'b0}}, J};  // Bit_Extender bit_extender_10
  assign bit_extender_11_out = {{6{1'b0}}, K};  // Bit_Extender bit_extender_11
  assign bit_extender_12_out = {{6{1'b0}}, L};  // Bit_Extender bit_extender_12
  assign bit_extender_13_out = {{6{1'b0}}, N};  // Bit_Extender bit_extender_13
  assign bit_extender_14_out = {{6{1'b0}}, O};  // Bit_Extender bit_extender_14
  DotMatrix #(.matrixcols(14), .matrixrows(8)) dotmatrix_1 (
    .col0(bit_extender_1_out), .col1(bit_extender_2_out), .col2(bit_extender_3_out),
    .col3(bit_extender_4_out), .col4(bit_extender_7_out), .col5(bit_extender_8_out),
    .col6(bit_extender_5_out), .col7(bit_extender_9_out), .col8(bit_extender_10_out),
    .col9(bit_extender_11_out), .col10(bit_extender_12_out), .col11(bit_extender_6_out),
    .col12(bit_extender_13_out), .col13(bit_extender_14_out));
  DotMatrix #(.matrixcols(1), .matrixrows(8)) dotmatrix_2 (.col0(Memo));
  Shift_Register #(.width(2), .length(3)) shift_register_2 (
    .in(A), .clk(clk), .q1(shift_register_2_q1));  // open: shift, out, load, clr, d0, q0, d1, d2, q2
  Comparator #(.width(4)) comparator_2 (.a(out_4), .b(4'b1111), .eq(isless));  // open: gt, lt
  Comparator #(.width(4)) comparator_3 (
    .a(Memo[3:0]), .b(bit_extender_15_out), .eq(comparator_3_eq), .lt(comparator_3_lt));  // open: gt
  assign bit_extender_15_out = {{2{1'b0}}, shift_register_2_q1};  // Bit_Extender bit_extender_15
  or or_2 (crash, comparator_3_eq, comparator_3_lt);

  // Notes on the sheet:
  //   contents of rom_1 (hex, n*v repeats v):
  //   1 1 4 4
endmodule
